# Fritzing sketch ms-kitchen (saved by Fritzing 0.9.3b)
circuit board: 4cm x 2cm
circuit board: 5cm x 7cm
breadboards: 1

parts:
  J1 = Screw terminal - 2 pins [part_number=input package=THT]
  J2 = Screw terminal - 2 pins [part_number=output package=THT]
  C1 = Electrolytic Capacitor [capacitance=100nF package="100 mil [THT, electrolytic]"]
  R1 = Resistor [tolerance=±5% resistance=470 package=THT]
  R3 = Resistor [tolerance=±5% resistance=100 package=THT]
  LED1 = LED - 3mm [color="Red (633nm)" package="3 mm [THT]"]
  U1 = Optocoupler [package=THT]
  R2 = Resistor [tolerance=±5% resistance=1k package=THT]
  JP1 = Header 3 [package=molex-1x3_lock]
  Mini_Pro_3v3 = Arduino Pro Mini (3.3V)
  R4 = Resistor [tolerance=±5% resistance=10k package=THT]
  Q1 = Basic FET N-Channel [package="TO220 [THT]"]
  U2 = MCP1702 Voltage Regulator [package="TO92 [THT]"]
  motion = Header 3 [package=molex-1x3_lock]
  temp/humi = Header 3 [package=molex-1x3_lock]
  S2 = SWITCH-MOMENTARY-2 [package=reed_switch_pth]
  C2 = Electrolytic Capacitor [capacitance=33µF package="100 mil [THT, electrolytic]"]
  C3 = Ceramic Capacitor [capacitance=1µF package="100 mil [THT, multilayer]"]
  radio = NRF24L01+ Breakout Board
  J3 = male pin header, 2 pins [form="♂ (male)"]
  J4 = male pin header, 2 pins [form="♂ (male)"]
  S1 = Square Pushbutton

nets (from the pcb view):
  N1: J1.pin1, J2.pin1, U1.Pin_5
  GND: J1.pin2, C1.-, LED1.cathode, U1.Pin_2, JP1.1, Mini_Pro_3v3.GND, R4.Pin_0, Q1.source, U2.GND, motion.1, temp/humi.1, S2.1, C2.-, C3.0, radio.GND, J3.pin1, J4.pin1, S1.leg0
  N2: J2.pin2, Q1.drain
  N3: C1.+, R1.Pin_1, U1.Pin_1
  N4: R1.Pin_0, JP1.2, Mini_Pro_3v3.D3
  N5: R3.Pin_0, U1.Pin_4, R2.Pin_0
  N6: R3.Pin_1, R4.Pin_1, Q1.gate
  N7: LED1.anode, R2.Pin_1
  VCC: Mini_Pro_3v3.VCC, U2.Vout, motion.3, temp/humi.3, C2.+, radio.VCC
  N8: Mini_Pro_3v3.D8, temp/humi.2
  N9: Mini_Pro_3v3.D7, motion.2
  N10: Mini_Pro_3v3.D4, S2.2, J4.pin2
  N11: Mini_Pro_3v3.D2, J3.pin2, S1.leg1
  N12: U2.Vin, C3.1

custom parts:
  MCP1702 Voltage Regulator: A MCP1702 Low Dropout Fixed Voltage Regulator (available in 1.2V, 1.5V, 1.8V, 2.5V, 2.8V, 3.0V, 3.3V, 4.0V, 5.0V)
