# Fritzing sketch ms-led-dimmer-rgbw (saved by Fritzing 0.9.3b)
circuit board: 4cm x 2cm
circuit board: 4cm x 2cm
breadboards: 1

parts:
  J1 = Screw terminal - 2 pins [part_number=input package=THT]
  J2 = Screw terminal - 2 pins [part_number=output package=THT]
  C1 = Electrolytic Capacitor [capacitance=100nF package="100 mil [THT, electrolytic]"]
  R1 = Resistor [tolerance=±5% resistance=470 package=THT]
  R3 = Resistor [tolerance=±5% resistance=100 package=THT]
  LED1 = LED - 3mm [color="Red (633nm)" package="3 mm [THT]"]
  U1 = Optocoupler [package=THT]
  R2 = Resistor [tolerance=±5% resistance=1k package=THT]
  JP1 = Header 3 [package=molex-1x3_lock]
  Part1 = Arduino Pro Mini (3.3V)
  R4 = Resistor [tolerance=±5% resistance=10k package=THT]
  Q1 = Basic FET N-Channel [package="TO220 [THT]"]
  U2 = MCP1702 Voltage Regulator [package="TO92 [THT]"]

nets:
  12V: J1.pin1, J2.pin1, U1.Pin_5, U2.Vin
  GND: J1.pin2, C1.-, LED1.cathode, U1.Pin_2, JP1.1, Part1.GND, R4.Pin_0, Q1.source, U2.GND
  N1: J2.pin2, Q1.drain
  N2: C1.+, R1.Pin_1, U1.Pin_1
  N3: R1.Pin_0, JP1.2, Part1.A0
  N4: R3.Pin_0, U1.Pin_4, R2.Pin_0
  N5: R3.Pin_1, R4.Pin_1, Q1.gate
  N6: LED1.anode, R2.Pin_1
  N7: Part1.VCC, U2.Vout

custom parts:
  MCP1702 Voltage Regulator: A MCP1702 Low Dropout Fixed Voltage Regulator (available in 1.2V, 1.5V, 1.8V, 2.5V, 2.8V, 3.0V, 3.3V, 4.0V, 5.0V)
