# Fritzing sketch ms-one-button (saved by Fritzing 0.9.3b)
circuit board: 5.7cm x 5.7cm
circuit board: 1.98877cm x 4.50056cm
circuit board: 0.775214cm x 1.96056cm

parts:
  BAT1 = Battery Holders [package=battcom_20mm_pth]
  C1 = Electrolytic Capacitor [capacitance=47µF voltage=16V package="100 mil [THT, electrolytic]"]
  MiniPro3v3 = Arduino Pro Mini (3.3V)
  RF24 = NRF24L01+ Breakout Board
  S1 = Round Pushbutton
  DHT1 = DHT11 Humitidy and Temperature Sensor  # not connected
  J1 = Piezo Speaker  # not connected

nets:
  N1: BAT1.+, MiniPro3v3.RAW
  GND: BAT1.-, C1.-, MiniPro3v3.GND, RF24.GND, S1.leg1
  VCC: C1.+, MiniPro3v3.VCC, RF24.VCC
  N2: MiniPro3v3.SCK, RF24.SCK
  N3: MiniPro3v3.MISO, RF24.MISO
  N4: MiniPro3v3.MOSI, RF24.MOSI
  N5: MiniPro3v3.D10, RF24.CS
  N6: MiniPro3v3.D9, RF24.CE
  N7: MiniPro3v3.D2, S1.leg0

custom parts:
  DHT11 Humitidy and Temperature Sensor: DHT11 Humidity and Temperature Sensor
