# Fritzing sketch ms-ir-sensor-4ch (saved by Fritzing 0.9.3b)
circuit board: 1.2cm x 3.2cm
circuit board: 1.2cm x 3.2cm
circuit board: 5.11922cm x 2.24903cm
circuit board: 1.2cm x 3.2cm
circuit board: 1.2cm x 3.2cm
breadboards: 1

parts:
  IR1 = IR Receiver Breakout [package=PCB]
  IR2 = IR Receiver Breakout [package=PCB]
  IR3 = IR Receiver Breakout [package=PCB]
  J1 = male pin header, 6 pins [form="♂ (male)"]
  IR4 = IR Receiver Breakout [package=PCB]

nets:
  GND: IR1.GND, IR2.GND, IR3.GND, J1.pin1, IR4.GND
  N1: IR1.OUT, J1.pin2
  VCC: IR1.VCC, IR2.VCC, IR3.VCC, J1.pin6, IR4.VCC
  N2: IR2.OUT, J1.pin3
  N3: IR3.OUT, J1.pin4
  N4: J1.pin5, IR4.OUT
