# Fritzing sketch ms-relay-switch-4ch (saved by Fritzing 0.9.3b)
circuit board: 5cm x 7cm
breadboards: 1

parts:
  Pro_Mini_5V = Arduino Pro Mini (3.3V)
  C2 = Electrolytic Capacitor [capacitance=47µF voltage=16V package="100 mil [THT, electrolytic]"]
  HLK-PM1 = HLK-PM01
  NRF24L01+ = NRF24L01+ Breakout Board
  AC_in = screw terminal, 2 pins [part_number="AC input"]
  U1 = MCP1702 Voltage Regulator [package="TO92 [THT]"]
  RELAY_out = male pin header, 6 pins [form="♂ (male)"]
  SENSORS_in = male pin header, 6 pins [form="♂ (male)"]
  C1 = Ceramic Capacitor [capacitance=100nF package="100 mil [THT, multilayer]"]

nets:
  N1: Pro_Mini_5V.RAW, HLK-PM1.+Vo, RELAY_out.pin6
  GND: Pro_Mini_5V.GND, C2.-, HLK-PM1.-Vo, NRF24L01+.GND, U1.GND, RELAY_out.pin1, SENSORS_in.pin1, C1.0
  VCC: Pro_Mini_5V.VCC, U1.Vin, C1.1
  N2: Pro_Mini_5V.A0, NRF24L01+.CE
  N3: Pro_Mini_5V.SCK, NRF24L01+.SCK
  N4: Pro_Mini_5V.MISO, NRF24L01+.MISO
  N5: Pro_Mini_5V.MOSI, NRF24L01+.MOSI
  N6: Pro_Mini_5V.D10, NRF24L01+.CS
  N7: Pro_Mini_5V.D9, RELAY_out.pin5
  N8: Pro_Mini_5V.D8, RELAY_out.pin4
  N9: Pro_Mini_5V.D7, RELAY_out.pin3
  N10: Pro_Mini_5V.D6, RELAY_out.pin2
  N11: Pro_Mini_5V.D5, SENSORS_in.pin2
  N12: Pro_Mini_5V.D4, SENSORS_in.pin3
  N13: Pro_Mini_5V.D3, SENSORS_in.pin4
  N14: Pro_Mini_5V.D2, SENSORS_in.pin5
  N15: C2.+, NRF24L01+.VCC, U1.Vout, SENSORS_in.pin6
  N16: HLK-PM1.AC#0, AC_in.pin2
  N17: HLK-PM1.AC#1, AC_in.pin1

notes:
  GND O1 O2 O3 O4 5V
  GND I1 I2 I3 I4 3V3

custom parts:
  MCP1702 Voltage Regulator: A MCP1702 Low Dropout Fixed Voltage Regulator (available in 1.2V, 1.5V, 1.8V, 2.5V, 2.8V, 3.0V, 3.3V, 4.0V, 5.0V)
