# Fritzing sketch ms-mini-3v3 (saved by Fritzing 0.9.3b)

parts:
  Part3 = NRF24L01+ Breakout Board
  Part4 = Arduino Pro Mini (3.3V)
  Part5 = FTDI Basic Programmer
  C8 = Electrolytic Capacitor [capacitance=47µF voltage=16V package="100 mil [THT, electrolytic]"]

nets:
  GND: Part3.GND, Part4.GND, Part5.CTS, Part5.GND, C8.-
  VCC: Part3.VCC, Part4.VCC, Part5.POWER, C8.+
  N1: Part3.CE, Part4.D9
  N2: Part3.CS, Part4.D10
  N3: Part3.SCK, Part4.SCK
  N4: Part3.MOSI, Part4.MOSI
  N5: Part3.MISO, Part4.MISO
  N6: Part4.DTR, Part5.DTR
  N7: Part4.TXO, Part5.RXI
  N8: Part4.RXI, Part5.TXO
